// Logisim project ex6ib.circ as structural Verilog: 1 circuit, main circuit main
module main (
  input  Y,
  input  Z,
  input  X,
  input  W
);

  wire and_1_out, and_2_out, and_3_out, nor_1_out, not_1_out, not_2_out, or_1_out, or_2_out, xnor_1_out,
       xor_1_out;

  not not_1 (not_1_out, Y);
  not not_2 (not_2_out, X);
  xnor xnor_1 (xnor_1_out, Y, Z);
  xor xor_1 (xor_1_out, X, W);
  and and_1 (and_1_out, not_1_out, Z);
  or or_1 (or_1_out, Z, not_2_out, W);
  and and_2 (and_2_out, not_1_out, not_2_out, W);
  nor nor_1 (nor_1_out, and_1_out, or_1_out, and_2_out);
  and and_3 (and_3_out, xnor_1_out, xor_1_out);
  or or_2 (or_2_out, nor_1_out, and_3_out);

  // Notes on the sheet:
  //   w6
  //   w7
  //   w4
  //   w5
  //   w1
  //   w2
  //   w3
  //   F2
  //   F1
  //   F3
endmodule
