// Logisim project ex6ic.circ as structural Verilog: 1 circuit, main circuit main
module main (
  input  A,
  input  B
);

  wire and_1_out, and_2_out, or_1_out;

  and and_1 (and_1_out, A, B);
  and and_2 (and_2_out, A, B);
  or or_1 (or_1_out, A, B);

  // Notes on the sheet:
  //   x1
  //   x2
  //   x3
endmodule
